// Logisim project D-latch.circ as structural Verilog: 1 circuit, main circuit main
module main (
  input  Data,
  input  Enabler
);

  wire And_2_out, And_out, NOR_2_out, NOR_out, NOT_out;

  not NOT (NOT_out, Data);
  and And (And_out, NOT_out, Enabler);
  and And_2 (And_2_out, Enabler, Data);
  nor NOR (NOR_out, And_out, NOR_2_out);
  nor NOR_2 (NOR_2_out, NOR_out, And_2_out);
  LED Q (.in(NOR_out));
  LED NOT_Q (.in(NOR_2_out));

  // Notes on the sheet:
  //   D LATCH
endmodule
