// Logisim project s-latch.circ as structural Verilog: 1 circuit, main circuit main
module main (
  input  R,
  input  S
);

  wire Nor_2_out, Nor_out;

  nor Nor (Nor_out, R, Nor_2_out);
  nor Nor_2 (Nor_2_out, Nor_out, S);
  LED Q (.in(Nor_out));
  LED Not_Q (.in(Nor_2_out));

  // Notes on the sheet:
  //   Reset
  //   set
  //   SR Latch
  //   Output
  //   Inverted output
endmodule
